# Fritzing sketch romi (saved by Fritzing 0.9.6b)
breadboards: 1

parts:
  PIC_left = PIC16F1705 [part_number=PIC16F1705 package="DIP (Dual Inline) [THT]"]
  PIC_right = PIC16F1705 [part_number=PIC16F1705 package="DIP (Dual Inline) [THT]"]
  SDA = Resistor [tolerance=±5% resistance=10000 power=0.25 package=THT]
  MCLR = Resistor [tolerance=±5% resistance=10000 power=0.25 package=THT]
  led_left = Resistor [tolerance=±5% resistance=1k power=0.25 package=THT]
  led_right = Resistor [tolerance=±5% resistance=1k power=0.25 package=THT]
  LED_left = LED - 3mm [color="Red (633nm)" current=0.030 package="3 mm [THT]"]
  LED_right = LED - 3mm [color="Red (633nm)" current=0.030 package="3 mm [THT]"]
  PWR_5v = Screw terminal - 2 pins [package=THT]
  U4 = PICKIT_3_PROG
  SCL = Resistor [tolerance=±5% resistance=10000 power=0.25 package=THT]
  RST = SWITCH-MOMENTARY-2 [package=tactile-pth]
  U5 = PICKIT_3_PROG
  U6 = MOTOR_HEADER
  U7 = MOTOR_HEADER
  RST/I2C = Camdenboss CTB0158-3 [part_number=CTB0158-3 package=THT]

nets:
  VDD: PIC_left.Vdd, PIC_right.Vdd, PIC_right.RC4, SDA.Pin_0, PWR_5v.pin1, U4.VDD, SCL.Pin_0, U5.VDD
  N1: PIC_left.RA5, U6.DIR
  N2: PIC_left.RA4, U6.PWM
  N3: PIC_left.MCLR/RA3, PIC_right.MCLR/RA3, MCLR.Pin_1, U4.Vpp/MCLR, RST.2, U5.Vpp/MCLR
  N4: PIC_left.RC5, U6.SLP
  VSS: PIC_left.RC4, PIC_left.RC2, PIC_right.RC2, led_left.Pin_0, led_right.Pin_0, PWR_5v.pin2, U4.VSS, RST.1, U5.VSS
  N5: PIC_left.RC3, LED_left.anode
  VSS_2: PIC_left.Vss, PIC_right.Vss, SCL.Pin_1, RST/I2C.pin2
  N6: PIC_left.RA0, PIC_right.RA0, SDA.Pin_1, RST/I2C.pin3
  N7: PIC_left.RA1, U6.B
  N8: PIC_left.RA2, U6.A
  N9: PIC_left.RC0, U4.PGC
  N10: PIC_left.RC1, U4.PGD
  N11: PIC_right.RA5, U7.DIR
  N12: PIC_right.RA4, U7.PWM
  N13: PIC_right.RC5, U7.SLP
  N14: PIC_right.RC3, LED_right.anode
  N15: PIC_right.RA1, U7.B
  N16: PIC_right.RA2, U7.A
  N17: PIC_right.RC0, U5.PGC
  N18: PIC_right.RC1, U5.PGD
  N19: MCLR.Pin_0, RST/I2C.pin1
  N20: led_left.Pin_1, LED_left.cathode
  N21: led_right.Pin_1, LED_right.cathode

custom parts:
  PIC16F1705: Microchip PIC16F1705
  PICKIT_3_PROG: PICKIT 3 6-pin inline header
  MOTOR_HEADER: Header for motor driver
